// Digital circuit alu.dig as structural Verilog
module alu (
  input  [7:0] a,
  input  [7:0] b,
  input  [3:0] op,
  output [7:0] out,
  output z_flag,
  output c_flag,
  output n_flag
);

  alu #(.applicationType("IVERILOG"), .CodeFile("alu.sv"), .iverilogOptions("-g2012")) u_alu (
    .a(a), .b(b), .op(op), .out(out), .z_flag(z_flag), .c_flag(c_flag), .n_flag(n_flag));
endmodule

/* Test case ALU testy:
a b op out z_flag c_flag n_flag
# ADD
59 49 0 108 0 0 0
200 100 0 44 0 1 0
128 128 0 0 1 1 0
# SUB
7 5 1 2 0 0 0
5 7 1 254 0 1 1
# INC / DEC
255 0 2 0 1 1 0
0 0 3 255 0 1 1
# AND OR XOR NOT
0xF0 0x3C 4 0x30 0 0 0
0xF0 0x0F 5 0xFF 0 0 1
0xAA 0xAA 6 0 1 0 0
0x0F 0 7 0xF0 0 0 1
# SHL SHR ROL
0x81 0 8 0x02 0 1 0
0x81 0 9 0x40 0 1 0
0x81 0 10 0x03 0 1 0
# CMP
3 3 11 3 1 0 0
2 9 11 2 0 0 1
9 2 11 9 0 1 0
# PASS_A CLR
42 0 12 42 0 0 0
42 0 13 0 1 0 0
*/
